# Fritzing sketch hitachi_display_i2c (saved by Fritzing 0.7.11b)
stripboards: 1

parts:
  U2 = atmega168 [package=dip]
  Y1 = Resonator [frequency="16 Mhz" package=THT]
  LCD1 = LCD screen
  R1 = Trimmer Potentiometer [maximum_resistance=10kΩ package=THT]
  J2 = male pin header, 6 pins [form="♂ (male)"]
  J3 = male pin header, 3 pins [form="♂ (male)"]
  J4 = male pin header, 3 pins [form="♂ (male)"]  # not connected

nets:
  N1: U2.RESET, J3.pin1
  N2: U2.D0_(RX), J2.pin6
  N3: U2.D1_(TX), J2.pin5
  N4: U2.VCC, R1.leg1
  N5: U2.GND#7, Y1.GND, R1.leg2
  N6: U2.XLAT1, Y1.pin_1
  N7: U2.XLAT2, Y1.0
  N8: U2.D8, LCD1.RS
  N9: U2.D12, J3.pin3
  N10: U2.D13, J3.pin2
  N11: U2.AVCC, J2.pin4
  N12: U2.GND#21, J2.pin3
  N13: U2.A0, J2.pin1
  N14: U2.A1, J2.pin2
